// Logisim project lab2.circ as structural Verilog: 1 circuit, main circuit 四位二进制可逆计数器
module \四位二进制可逆计数器  (
  input  in_1,
  input  in_2,
  input  in_3,
  output out_4,
  output out_5,
  output out_6,
  output out_7
);

  wire and_1_out, and_2_out, and_3_out, and_4_out, and_5_out, and_6_out, and_7_out, and_8_out, clock_1_out,
       not_1_out, not_2_out, not_3_out, nQA, nQB, nQC, nQD, or_1_out, or_2_out, or_3_out, or_4_out, or_5_out,
       xor_1_out, xor_2_out, xor_3_out, xor_4_out, xor_5_out, xor_6_out, xor_7_out;

  and and_1 (and_1_out, out_7, out_6, out_5);
  or or_1 (or_1_out, out_7, out_6, out_5);
  and and_2 (and_2_out, out_7, out_6);
  or or_2 (or_2_out, out_7, out_6);
  xor xor_1 (xor_1_out, out_4, and_1_out);
  not not_1 (not_1_out, out_4);
  xor xor_2 (xor_2_out, not_1_out, or_1_out);
  xor xor_3 (xor_3_out, out_5, and_2_out);
  not not_2 (not_2_out, out_5);
  xor xor_4 (xor_4_out, not_2_out, or_2_out);
  xor xor_5 (xor_5_out, out_7, out_6);
  not not_3 (not_3_out, out_7);
  xor xor_6 (xor_6_out, not_3_out, out_6);
  and and_3 (and_3_out, in_1, xor_1_out);
  and and_4 (and_4_out, in_3, xor_2_out);
  and and_5 (and_5_out, in_1, xor_3_out);
  and and_6 (and_6_out, in_3, xor_4_out);
  and and_7 (and_7_out, in_1, xor_5_out);
  and and_8 (and_8_out, in_3, xor_6_out);
  Clock clock_1 (.out(clock_1_out));
  or or_3 (or_3_out, and_3_out, and_4_out);
  or or_4 (or_4_out, and_5_out, and_6_out);
  or or_5 (or_5_out, and_7_out, and_8_out);
  D_Flip_Flop D (.clk(clock_1_out), .D(or_3_out), .Q(out_4), .Qn(nQD), .en(xor_7_out), .reset(in_2));  // open: preset
  D_Flip_Flop C (.clk(clock_1_out), .D(or_4_out), .Q(out_5), .Qn(nQC), .en(xor_7_out), .reset(in_2));  // open: preset
  D_Flip_Flop B (.clk(clock_1_out), .D(or_5_out), .Q(out_6), .Qn(nQB), .en(xor_7_out), .reset(in_2));  // open: preset
  D_Flip_Flop A (.clk(clock_1_out), .D(nQA), .Q(out_7), .Qn(nQA), .en(xor_7_out), .reset(in_2));  // open: preset
  xor xor_7 (xor_7_out, in_1, in_3);
  LED led_1 (.in(xor_7_out));

  // Other names for the same wires on the sheet: CLR = in_2; CPD = in_3; CPU = in_1; QA = out_7; QB = out_6;
  //   QC = out_5; QD = out_4

  // Notes on the sheet:
  //   绿灯表示正常运行
endmodule
